# Fritzing sketch Bluetooth-Led (saved by Fritzing 0.8.7b)
breadboards: 1

parts:
  Parte1 = Arduino Uno (Rev3)
  Parte2 = JY-MCU
  R1 = Resistor [tolerance=±5% resistance=220 package=THT]
  LED1 = LED - 5mm [color="Red (633nm)" package="5 mm [THT]"]

nets:
  N1: Parte1.D9_PWM, Parte2.VCC
  N2: Parte1.D10_PWM/SS, Parte2.TX
  N3: Parte1.D11_PWM/MOSI, Parte2.RX
  GND: Parte1.GND, Parte2.GND, LED1.cathode
  N4: Parte1.D7, R1.Pin_0
  N5: R1.Pin_1, LED1.anode

custom parts:
  JY-MCU: Description: The Bluetooth Mate is very similar to our BlueSMiRF modem, but it is designed specifically to be used with our Arduino Pros and LilyPad Arduinos. These modems work as a serial (RX/TX) pipe, and are a great wireless replacement for serial cables. Any serial stream from 9600 to 115200bps can be passed seamlessly from your computer to your target. Bluetooth Mate has the same pin out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
