# Fritzing sketch Rover-Bluetooth (saved by Fritzing 0.8.7b)

parts:
  Parte1 = Arduino Uno (Rev3)
  Parte2 = JY-MCU
  motorcontrollerDRI1 = motorcontrollerDRI0002
  M1 = DC Motor
  M2 = DC Motor
  M4 = DC Motor
  M3 = DC Motor

nets:
  N1: Parte1.D8, Parte2.VCC
  N2: Parte1.D10_PWM/SS, Parte2.TX
  N3: Parte1.D11_PWM/MOSI, Parte2.RX
  N4: Parte1.D4, motorcontrollerDRI1.M1
  N5: Parte1.D5_PWM, motorcontrollerDRI1.E1
  N6: Parte1.D6_PWM, motorcontrollerDRI1.E2
  N7: Parte1.D7, motorcontrollerDRI1.M2
  GND: Parte1.GND, Parte2.GND
  N8: motorcontrollerDRI1.M1-, M1.pin_1, M2.pin_1
  N9: motorcontrollerDRI1.M1+, M1.pin_2, M2.pin_2
  N10: motorcontrollerDRI1.M2+, M4.pin_2, M3.pin_2
  N11: motorcontrollerDRI1.M2-, M4.pin_1, M3.pin_1

custom parts:
  JY-MCU: Description: The Bluetooth Mate is very similar to our BlueSMiRF modem, but it is designed specifically to be used with our Arduino Pros and LilyPad Arduinos. These modems work as a serial (RX/TX) pipe, and are a great wireless replacement for serial cables. Any serial stream from 9600 to 115200bps can be passed seamlessly from your computer to your target. Bluetooth Mate has the same pin out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
