# Fritzing sketch Rover-Infrared (saved by Fritzing 0.8.7b)

parts:
  Parte1 = Arduino Uno (Rev3)
  motorcontrollerDRI1 = motorcontrollerDRI0002
  M1 = DC Motor
  M2 = DC Motor
  M4 = DC Motor
  M3 = DC Motor
  U1 = QRE1113 [package=qre1113]
  U2 = QRE1113 [package=qre1113]

nets:
  N1: Parte1.A0, U1.A
  N2: Parte1.A1, U2.A
  N3: Parte1.D10_PWM/SS, U1.C
  N4: Parte1.D11_PWM/MOSI, U2.C
  N5: Parte1.D4, motorcontrollerDRI1.M1
  N6: Parte1.D5_PWM, motorcontrollerDRI1.E1
  N7: Parte1.D6_PWM, motorcontrollerDRI1.E2
  N8: Parte1.D7, motorcontrollerDRI1.M2
  N9: Parte1.GND, U1.K, U1.E, U2.K, U2.E
  N10: motorcontrollerDRI1.M1-, M1.pin_1, M2.pin_1
  N11: motorcontrollerDRI1.M1+, M1.pin_2, M2.pin_2
  N12: motorcontrollerDRI1.M2+, M4.pin_2, M3.pin_2
  N13: motorcontrollerDRI1.M2-, M4.pin_1, M3.pin_1
